// Logisim project ALU.circ as structural Verilog: 1 circuit, main circuit ALU
module ALU (
  input  [31:0] A,
  input  [31:0] B,
  input  [4:0] Shift,
  input  CarryIn,
  input  [3:0] Codop,
  output [31:0] S,
  output [3:0] Flags
);

  wire and_3_out, and_4_out, and_5_out, and_6_out, and_7_out, and_8_out, and_9_out, and_10_out,
       bitselector_1_out, bitselector_2_out, bitselector_3_out, bitselector_4_out, bitselector_5_out,
       bitselector_6_out, bitselector_7_out, bitselector_8_out, bitselector_9_out, bitselector_10_out,
       bitselector_11_out, bitselector_12_out, C1, C2, C3, C4, N1, not_3_out, not_4_out, not_5_out,
       not_6_out, not_7_out, not_8_out, not_9_out, not_10_out, not_11_out, not_12_out, not_13_out,
       not_14_out, V_ADC, V_CMN, V_CMP, V_SBC;
  wire [31:0] ADC, AND_6156fd2f, ASR, BIC, bit_extender_1_out, bit_extender_2_out, bit_extender_3_out, CMN,
       CMP, EOR, LSL, LSR, MUL, MVN, not_1_out, ORR, ROR_edf90693, RSB, SBC, subtractor_2_out;

  assign AND_6156fd2f = A & B;  // AND_Gate and_1, 32 bits wide
  assign not_1_out = ~B;  // NOT_Gate not_1, 32 bits wide
  assign BIC = A & not_1_out;  // AND_Gate and_2, 32 bits wide
  assign ORR = A | B;  // OR_Gate or_1, 32 bits wide
  assign MVN = ~B;  // NOT_Gate not_2, 32 bits wide
  assign EOR = A ^ B;  // XOR_Gate xor_1, 32 bits wide
  Adder #(.width(32)) adder_1 (.a(A), .b(B), .out(ADC), .cin(CarryIn), .cout(C1));
  assign bit_extender_1_out = {{31{1'b0}}, 1'b0};  // Bit_Extender bit_extender_1
  Adder #(.width(32)) adder_2 (.a(A), .b(B), .out(CMN), .cin(1'b0), .cout(C4));
  Subtractor #(.width(32)) subtractor_1 (.a(bit_extender_1_out), .b(B), .out(RSB), .bin(1'b0));  // open: bout
  Shifter #(.width(32)) shifter_1 (.in(B), .\dist (Shift), .out(LSL));
  assign bit_extender_2_out = {{31{1'b0}}, 1'b0};  // Bit_Extender bit_extender_2
  Shifter #(.width(32), .shift("lr")) shifter_2 (.in(B), .\dist (Shift), .out(LSR));
  Subtractor #(.width(32)) subtractor_2 (.a(A), .b(B), .out(subtractor_2_out), .bin(1'b1), .bout(N1));
  Subtractor #(.width(32)) subtractor_3 (.a(A), .b(B), .out(CMP), .bin(1'b0), .bout(C3));
  Multiplier #(.width(32)) multiplier_1 (.a(A), .b(B), .out(MUL), .cin(bit_extender_2_out));  // open: cout
  Shifter #(.width(32), .shift("ar")) shifter_3 (.in(B), .\dist (Shift), .out(ASR));
  Adder #(.width(32)) adder_3 (.a(subtractor_2_out), .b(bit_extender_3_out), .out(SBC), .cin(1'b0), .cout(C2));
  assign bit_extender_3_out = {{31{1'b0}}, CarryIn};  // Bit_Extender bit_extender_3
  Multiplexer #(.select(4), .width(32), .enable("false")) multiplexer_1 (
    .in0(AND_6156fd2f), .in1(EOR), .in2(LSL), .in3(LSR), .in4(ASR), .in5(ADC), .in6(SBC), .in7(ROR_edf90693),
    .in8(AND_6156fd2f), .in9(RSB), .in10(CMP), .in11(CMN), .in12(ORR), .in13(MUL), .in14(BIC), .in15(MVN),
    .out({Flags[0], S[30:0]}), .sel(Codop));
  Shifter #(.width(32), .shift("rr")) shifter_4 (.in(B), .\dist (Shift), .out(ROR_edf90693));
  Multiplexer #(.select(4), .enable("false")) multiplexer_2 (
    .in0(1'b0), .in1(1'b0), .in2(1'b0), .in3(1'b0), .in4(1'b0), .in5(C1), .in6(C2), .in7(1'b0), .in8(1'b0),
    .in9(1'b0), .in10(C3), .in11(C4), .in12(1'b0), .in13(1'b0), .in14(1'b0), .in15(1'b0), .out(Flags[2]),
    .sel(Codop));
  BitSelector #(.width(32)) bitselector_1 (.in(ADC), .out(bitselector_1_out), .sel({5{1'b1}}));
  BitSelector #(.width(32)) bitselector_2 (.in(CMN), .out(bitselector_2_out), .sel({5{1'b1}}));
  Comparator #(.width(32)) comparator_1 (.a({32{1'b0}}), .b({Flags[0], S[30:0]}), .eq(Flags[1]));  // open: gt, lt
  BitSelector #(.width(32)) bitselector_3 (.in(A), .out(bitselector_3_out), .sel({5{1'b1}}));
  BitSelector #(.width(32)) bitselector_4 (.in(B), .out(bitselector_4_out), .sel({5{1'b1}}));
  BitSelector #(.width(32)) bitselector_5 (.in(A), .out(bitselector_5_out), .sel({5{1'b1}}));
  BitSelector #(.width(32)) bitselector_6 (.in(B), .out(bitselector_6_out), .sel({5{1'b1}}));
  Multiplexer #(.select(4), .enable("false")) multiplexer_3 (
    .in0(V_CMN), .in1(V_CMN), .in2(V_CMN), .in3(V_CMN), .in4(V_CMN), .in5(V_ADC), .in6(V_SBC), .in7(V_CMN),
    .in8(V_CMN), .in9(V_CMN), .in10(V_CMP), .in11(V_CMN), .in12(V_CMN), .in13(V_CMN), .in14(V_CMN),
    .in15(V_CMN), .out(Flags[3]), .sel(Codop));
  not not_3 (not_3_out, bitselector_1_out);
  and and_3 (and_3_out, not_3_out, not_4_out, bitselector_4_out);
  not not_4 (not_4_out, bitselector_3_out);
  and and_4 (and_4_out, bitselector_1_out, bitselector_3_out, not_5_out);
  not not_5 (not_5_out, bitselector_4_out);
  not not_6 (not_6_out, bitselector_2_out);
  not not_7 (not_7_out, bitselector_5_out);
  and and_5 (and_5_out, not_6_out, not_7_out, bitselector_6_out);
  and and_6 (and_6_out, bitselector_2_out, bitselector_5_out, not_8_out);
  not not_8 (not_8_out, bitselector_6_out);
  or or_2 (V_ADC, and_3_out, and_4_out);
  or or_3 (V_CMN, and_5_out, and_6_out);
  BitSelector #(.width(32)) bitselector_7 (.in(SBC), .out(bitselector_7_out), .sel({5{1'b1}}));
  BitSelector #(.width(32)) bitselector_8 (.in(CMP), .out(bitselector_8_out), .sel({5{1'b1}}));
  BitSelector #(.width(32)) bitselector_9 (.in(A), .out(bitselector_9_out), .sel({5{1'b1}}));
  BitSelector #(.width(32)) bitselector_10 (.in(B), .out(bitselector_10_out), .sel({5{1'b1}}));
  BitSelector #(.width(32)) bitselector_11 (.in(A), .out(bitselector_11_out), .sel({5{1'b1}}));
  BitSelector #(.width(32)) bitselector_12 (.in(B), .out(bitselector_12_out), .sel({5{1'b1}}));
  not not_9 (not_9_out, bitselector_7_out);
  and and_7 (and_7_out, not_9_out, bitselector_9_out, bitselector_10_out);
  and and_8 (and_8_out, bitselector_7_out, not_10_out, not_11_out);
  not not_10 (not_10_out, bitselector_9_out);
  not not_11 (not_11_out, bitselector_10_out);
  not not_12 (not_12_out, bitselector_8_out);
  and and_9 (and_9_out, not_12_out, bitselector_11_out, bitselector_12_out);
  and and_10 (and_10_out, bitselector_8_out, not_13_out, not_14_out);
  not not_13 (not_13_out, bitselector_11_out);
  not not_14 (not_14_out, bitselector_12_out);
  or or_4 (V_SBC, and_7_out, and_8_out);
  or or_5 (V_CMP, and_9_out, and_10_out);

  assign S[31] = Flags[0];
  // also tied to GND on the sheet: V_CMN

  // Other names for the same wires on the sheet: Z = Flags[1]; C = Flags[2]; V = Flags[3]; N = Flags[0];
  //   TST[31:0] = AND_6156fd2f

  // Notes on the sheet:
  //   Note: for ROR, C = N
  //   Note 2: assume that shift > 0 for LSL and LSR
  //   Note: for ROR, C = N
endmodule
