// Logisim project BancDeRegistres.circ as structural Verilog: 1 circuit, main circuit BancRegistre
module BancRegistre (
  input  [31:0] DataIn,
  input  [2:0] RegDest,
  input  Clk,
  input  Reset,
  input  [2:0] RegA,
  input  [2:0] RegB,
  output [31:0] AOut,
  output [31:0] BOut,
  output [31:0] R0,
  output [31:0] R1,
  output [31:0] R2,
  output [31:0] R3,
  output [31:0] R4,
  output [31:0] R5,
  output [31:0] R6,
  output [31:0] R7
);

  wire and_2_out, and_3_out, and_4_out, not_1_out, not_2_out, not_3_out, store, W0, W1, W2, W3, W4, W5, W6,
       W7;
  wire [2:0] and_5_out, bit_extender_1_out, or_1_out;

  and and_1 (store, and_2_out, DataIn[15]);
  and and_2 (and_2_out, and_3_out, not_1_out);
  and and_3 (and_3_out, and_4_out, not_3_out);
  not not_1 (not_1_out, DataIn[14]);
  not not_2 (not_2_out, DataIn[11]);
  and and_4 (and_4_out, not_2_out, DataIn[12]);
  not not_3 (not_3_out, DataIn[13]);
  Decoder #(.select(3)) decoder_1 (
    .out0(W0), .out1(W1), .out2(W2), .out3(W3), .out4(W4), .out5(W5), .out6(W6), .out7(W7), .sel(RegDest),
    .en(1'b1));
  assign bit_extender_1_out = {{2{store}}, store};  // Bit_Extender bit_extender_1
  assign and_5_out = bit_extender_1_out & RegDest;  // AND_Gate and_5, 3 bits wide
  assign or_1_out = and_5_out | RegA;  // OR_Gate or_1, 3 bits wide
  Multiplexer #(.select(3), .width(32), .enable("false")) multiplexer_1 (
    .in0(R0), .in1(R1), .in2(R2), .in3(R3), .in4(R4), .in5(R5), .in6(R6), .in7(R7), .out(AOut), .sel(or_1_out));
  Multiplexer #(.select(3), .width(32), .enable("false")) multiplexer_2 (
    .in0(R0), .in1(R1), .in2(R2), .in3(R3), .in4(R4), .in5(R5), .in6(R6), .in7(R7), .out(BOut), .sel(RegB));
  Register #(.width(32), .trigger("falling")) register_1 (.D(DataIn), .en(W0), .clk(Clk), .Q(R0), .clr(Reset));
  Register #(.width(32), .trigger("falling")) register_2 (.D(DataIn), .en(W1), .clk(Clk), .Q(R1), .clr(Reset));
  Register #(.width(32), .trigger("falling")) register_3 (.D(DataIn), .en(W2), .clk(Clk), .Q(R2), .clr(Reset));
  Register #(.width(32), .trigger("falling")) register_4 (.D(DataIn), .en(W3), .clk(Clk), .Q(R3), .clr(Reset));
  Register #(.width(32), .trigger("falling")) register_5 (.D(DataIn), .en(W4), .clk(Clk), .Q(R4), .clr(Reset));
  Register #(.width(32), .trigger("falling")) register_6 (.D(DataIn), .en(W5), .clk(Clk), .Q(R5), .clr(Reset));
  Register #(.width(32), .trigger("falling")) register_7 (.D(DataIn), .en(W6), .clk(Clk), .Q(R6), .clr(Reset));
  Register #(.width(32), .trigger("falling")) register_8 (.D(DataIn), .en(W7), .clk(Clk), .Q(R7), .clr(Reset));
endmodule
