// Logisim project Controller.circ as structural Verilog: 10 circuits, main circuit Controller
module Controller (
  input  [15:0] Inst,
  input  [3:0] Flags,
  input  Clk,
  input  Reset,
  output Carry,
  output DP_Shift,
  output Imm32_Enable,
  output [4:0] Imm5,
  output [31:0] Imm32,
  output [3:0] ALU_Opcode,
  output [2:0] Rm,
  output [2:0] Rn,
  output [2:0] Rd,
  output [31:0] RAM_Addr,
  output Load,
  output Store,
  output [7:0] PC
);

  wire Conditional_1_verified, Load_Store_1_pc_hold, not_1_out, Opcode_Decoder_1_conditional,
       Opcode_Decoder_1_data_processing, Opcode_Decoder_1_load_store, Opcode_Decoder_1_shift,
       Opcode_Decoder_1_sp_address, Shift_Add_Sub_Mov_1_carry, SP_Address_1_write_enable;
  wire [2:0] Data_Processing_1_rd, Data_Processing_1_rm, Data_Processing_1_rn, Load_Store_1_rd,
       Load_Store_1_rm, Shift_Add_Sub_Mov_1_rd, Shift_Add_Sub_Mov_1_rm, Shift_Add_Sub_Mov_1_rn;
  wire [3:0] Data_Processing_1_alu_opcode, Data_Processing_1_flags_update_mask, flags_apsr_1_flags_out,
       or_1_out, Shift_Add_Sub_Mov_1_alu_opcode, Shift_Add_Sub_Mov_1_flags_update_mask;
  wire [7:0] adder_1_out, adder_2_out, Conditional_1_offset, register_1_q;
  wire [31:0] SP_Address_1_new_stack_pointer, Stack_Pointer_q;

  Register #(.width(32)) Stack_Pointer (
    .D(SP_Address_1_new_stack_pointer), .en(SP_Address_1_write_enable), .clk(Clk), .Q(Stack_Pointer_q),
    .clr(Reset));
  Opcode_Decoder Opcode_Decoder_1 (
    .Opcode(Inst[15:10]), .Shift(Opcode_Decoder_1_shift), .Data_Processing(Opcode_Decoder_1_data_processing),
    .Load_Store(Opcode_Decoder_1_load_store), .SP_Address(Opcode_Decoder_1_sp_address),
    .Conditional(Opcode_Decoder_1_conditional));
  assign or_1_out = Data_Processing_1_flags_update_mask | Shift_Add_Sub_Mov_1_flags_update_mask;  // OR_Gate or_1, 4 bits wide
  Shift_Add_Sub_Mov Shift_Add_Sub_Mov_1 (
    .Imm32_Enable(Imm32_Enable), .ALU_Opcode(Shift_Add_Sub_Mov_1_alu_opcode), .Instruction(Inst),
    .Enable(Opcode_Decoder_1_shift), .Carry(Shift_Add_Sub_Mov_1_carry),
    .Flags_Update_Mask(Shift_Add_Sub_Mov_1_flags_update_mask), .Rd(Shift_Add_Sub_Mov_1_rd),
    .Rn(Shift_Add_Sub_Mov_1_rn), .Rm(Shift_Add_Sub_Mov_1_rm), .Imm5(Imm5), .Imm32(Imm32));
  Data_Processing Data_Processing_1 (
    .Rn(Data_Processing_1_rn), .Instruction(Inst), .Rd(Data_Processing_1_rd), .Rm(Data_Processing_1_rm),
    .ALU_Opcode(Data_Processing_1_alu_opcode), .Flags_Update_Mask(Data_Processing_1_flags_update_mask),
    .Enable(Opcode_Decoder_1_data_processing));
  Flags_APSR flags_apsr_1 (
    .Flags_In(or_1_out), .Update_Mask(Flags), .Clk(Clk), .Rst(Reset), .Flags_Out(flags_apsr_1_flags_out));
  Load_Store Load_Store_1 (
    .Load(Load), .Store(Store), .Enable(Opcode_Decoder_1_load_store), .Rm(Load_Store_1_rm),
    .Rd(Load_Store_1_rd), .Stack_Pointer(Stack_Pointer_q), .RAM_Addr(RAM_Addr), .Instruction(Inst),
    .Clk(Clk), .Reset(Reset), .PC_Hold(Load_Store_1_pc_hold));
  Conditional Conditional_1 (
    .Offset(Conditional_1_offset), .Enable(Opcode_Decoder_1_conditional), .Verified(Conditional_1_verified),
    .N(flags_apsr_1_flags_out[3]), .Z(flags_apsr_1_flags_out[2]), .C(flags_apsr_1_flags_out[1]),
    .V(flags_apsr_1_flags_out[0]), .Instruction(Inst));
  SP_Address SP_Address_1 (
    .New_Stack_Pointer(SP_Address_1_new_stack_pointer), .Stack_Pointer(Stack_Pointer_q),
    .Enable(Opcode_Decoder_1_sp_address), .Instruction(Inst), .Write_Enable(SP_Address_1_write_enable));
  Adder adder_1 (.a(8'h3), .b(Conditional_1_offset), .out(adder_1_out), .cin(1'b0));  // open: cout
  Register register_1 (.D(adder_2_out), .en(1'b1), .clk(Clk), .Q(register_1_q), .clr(Reset));
  Adder adder_2 (.a(adder_1_out), .b(PC), .out(adder_2_out), .cin(1'b0));  // open: cout
  and and_1 (DP_Shift, Opcode_Decoder_1_shift, ~Opcode_Decoder_1_data_processing);  // AND_Gate
  not not_1 (not_1_out, Load_Store_1_pc_hold);
  Counter #(.trigger("falling")) counter_1 (
    .clr(Reset), .load(Conditional_1_verified), .up(1'b1), .count(not_1_out), .clk(Clk), .D(register_1_q),
    .Q(PC));  // open: carry
  Multiplexer #(.enable("false")) multiplexer_1 (
    .in0(flags_apsr_1_flags_out[1]), .in1(Shift_Add_Sub_Mov_1_carry), .out(Carry), .sel(DP_Shift));
  assign ALU_Opcode = Shift_Add_Sub_Mov_1_alu_opcode | Data_Processing_1_alu_opcode;  // OR_Gate or_2, 4 bits wide
  assign Rm = Shift_Add_Sub_Mov_1_rm | Data_Processing_1_rm | Load_Store_1_rm;  // OR_Gate or_3, 3 bits wide
  assign Rn = Shift_Add_Sub_Mov_1_rn | Data_Processing_1_rn;  // OR_Gate or_4, 3 bits wide
  assign Rd = Shift_Add_Sub_Mov_1_rd | Data_Processing_1_rd | Load_Store_1_rd;  // OR_Gate or_5, 3 bits wide

  // Notes on the sheet:
  //   Extract Opcode
  //   Extract carry
  //   Ajout d'un registre car le compteur est en flanc descendant, et l'offset ne s'ajoute pas
  //   IF Reg_Imm=1 THEN use shift value from register ELSE use shift value from Imm5
  //   Add 3 to offset because ARM pre-increments PC
  //   and does an additionnal prefect operation
  //   Buffer flags for next instruction
  //   Le compteur a été passé en flanc descendant parcequ'il s'incrémentait dès le tick d'horloge, passant la première instruction
endmodule

module Conditional (
  input  Enable,
  input  N,
  input  Z,
  input  C,
  input  V,
  input  [15:0] Instruction,
  output [7:0] Offset,
  output Verified
);

  wire and_1_out, and_2_out, and_3_out, multiplexer_2_out, not_1_out, not_2_out, not_3_out, not_4_out,
       not_5_out, not_6_out, not_7_out, or_1_out, xnor_1_out, xor_1_out, xor_2_out;
  wire [3:0] selec;
  wire [7:0] bitselector_2_out;

  BitSelector #(.width(16), .group(4)) bitselector_1 (.in(Instruction), .out(selec), .sel(2'b10));
  BitSelector #(.width(16), .group(8)) bitselector_2 (.in(Instruction), .out(bitselector_2_out), .sel(1'b0));
  Multiplexer #(.width(8), .enable("false")) multiplexer_1 (
    .in0({8{1'b0}}), .in1(bitselector_2_out), .out(Offset), .sel(Enable));
  not not_1 (not_1_out, Z);
  not not_2 (not_2_out, Z);
  and and_1 (and_1_out, C, not_2_out);
  not not_3 (not_3_out, V);
  not not_4 (not_4_out, N);
  not not_5 (not_5_out, C);
  Multiplexer #(.select(4), .enable("false")) multiplexer_2 (
    .in0(Z), .in1(not_1_out), .in2(C), .in3(not_5_out), .in4(N), .in5(not_4_out), .in6(V), .in7(not_3_out),
    .in8(and_1_out), .in9(and_2_out), .in10(xnor_1_out), .in11(xor_1_out), .in12(and_3_out), .in13(or_1_out),
    .in14(1'b1), .out(multiplexer_2_out), .sel(selec));  // open: in15
  Multiplexer #(.enable("false")) multiplexer_3 (.in0(1'b0), .in1(multiplexer_2_out), .out(Verified), .sel(Enable));
  xnor xnor_1 (xnor_1_out, V, N);
  not not_6 (not_6_out, C);
  and and_2 (and_2_out, not_6_out, Z);
  and and_3 (and_3_out, xnor_1_out, not_7_out);
  xor xor_1 (xor_1_out, N, V);
  xor xor_2 (xor_2_out, V, Z);
  not not_7 (not_7_out, Z);
  or or_1 (or_1_out, xor_2_out, Z);

  // Notes on the sheet:
  //   Z
  //   N
  //   V
  //   C
endmodule

module Opcode_Decoder (
  input  [5:0] Opcode,
  output Shift,
  output Data_Processing,
  output Load_Store,
  output SP_Address,
  output Conditional
);

  wire not_1_out, not_2_out, not_3_out, not_4_out, not_5_out, not_6_out, not_7_out, not_8_out, not_9_out,
       not_10_out, not_11_out;

  not not_1 (not_1_out, Opcode[5]);
  not not_2 (not_2_out, Opcode[4]);
  not not_3 (not_3_out, Opcode[5]);
  not not_4 (not_4_out, Opcode[3]);
  not not_5 (not_5_out, Opcode[2]);
  not not_6 (not_6_out, Opcode[1]);
  not not_7 (not_7_out, Opcode[0]);
  not not_8 (not_8_out, Opcode[4]);
  not not_9 (not_9_out, Opcode[3]);
  not not_10 (not_10_out, Opcode[4]);
  not not_11 (not_11_out, Opcode[3]);
  and and_1 (Shift, not_1_out, not_2_out);
  and and_2 (Data_Processing, not_3_out, Opcode[4], not_4_out, not_5_out, not_6_out, not_7_out);
  and and_3 (Load_Store, Opcode[5], not_8_out, not_9_out, Opcode[2]);
  and and_4 (SP_Address, Opcode[5], not_10_out, Opcode[3], Opcode[2]);
  and and_5 (Conditional, Opcode[5], Opcode[4], not_11_out, Opcode[2]);

  // Other names for the same wires on the sheet: B0 = Opcode[0]; B1 = Opcode[1]; B2 = Opcode[2]; B3 = Opcode[3];
  //   B4 = Opcode[4]; B5 = Opcode[5]

  // Notes on the sheet:
  //   Shift, add, sub, mov
  //   Load/Store
  //   Data Processing
  //   SP Address
  //   Conditional branch
endmodule

module Data_Processing (
  input  [15:0] Instruction,
  input  Enable,
  output [2:0] Rn,
  output [2:0] Rd,
  output [2:0] Rm,
  output [3:0] ALU_Opcode,
  output [3:0] Flags_Update_Mask
);

  wire ADDC, ASR, BAND, BC, BN, CN, CR, EOR, LOR, LSL, LSR, MTR, not_1_out, not_2_out, not_3_out, not_4_out,
       or_1_out, or_2_out, RR, RS, SFA, SUBC;
  wire [1:0] or_6_out;
  wire [2:0] and_17_out, and_18_out, and_19_out, bit_extender_1_out, bit_extender_2_out, bit_extender_3_out,
       RD_t, RN_t;

  not not_1 (not_1_out, Instruction[8]);
  not not_2 (not_2_out, Instruction[7]);
  not not_3 (not_3_out, Instruction[6]);
  not not_4 (not_4_out, Instruction[9]);
  and and_1 (BAND, not_3_out, not_2_out, not_1_out, not_4_out);
  and and_2 (EOR, Instruction[6], not_2_out, not_1_out, not_4_out);
  and and_3 (LSL, not_3_out, Instruction[7], not_1_out, not_4_out);
  and and_4 (LSR, Instruction[6], Instruction[7], not_1_out, not_4_out);
  and and_5 (ASR, not_3_out, not_2_out, Instruction[8], not_4_out);
  and and_6 (ADDC, Instruction[6], not_2_out, Instruction[8], not_4_out);
  and and_7 (SUBC, not_3_out, Instruction[7], Instruction[8], not_4_out);
  and and_8 (RR, Instruction[6], Instruction[7], Instruction[8], not_4_out);
  and and_9 (SFA, not_3_out, not_2_out, not_1_out, Instruction[9]);
  and and_10 (RS, Instruction[6], not_2_out, not_1_out, Instruction[9]);
  and and_11 (CR, not_3_out, Instruction[7], not_1_out, Instruction[9]);
  and and_12 (CN, Instruction[6], Instruction[7], not_1_out, Instruction[9]);
  and and_13 (LOR, not_3_out, not_2_out, Instruction[8], Instruction[9]);
  and and_14 (MTR, Instruction[6], not_2_out, Instruction[8], Instruction[9]);
  and and_15 (BC, not_3_out, Instruction[7], Instruction[8], Instruction[9]);
  and and_16 (BN, Instruction[6], Instruction[7], Instruction[8], Instruction[9]);
  or or_1 (or_1_out, SFA, CR, CN);
  assign bit_extender_1_out = {{2{BN}}, BN};  // Bit_Extender bit_extender_1
  or or_2 (or_2_out, BAND, EOR, LSL, LSR, ASR, ADDC, SUBC, RR, LOR, BC, RS, MTR);
  assign bit_extender_2_out = {{2{or_1_out}}, or_1_out};  // Bit_Extender bit_extender_2
  assign and_17_out = bit_extender_1_out & Instruction[2:0];  // AND_Gate and_17, 3 bits wide
  assign bit_extender_3_out = {{2{or_2_out}}, or_2_out};  // Bit_Extender bit_extender_3
  assign and_18_out = bit_extender_2_out & Instruction[2:0];  // AND_Gate and_18, 3 bits wide
  assign and_19_out = bit_extender_3_out & Instruction[2:0];  // AND_Gate and_19, 3 bits wide
  assign RD_t = and_19_out | and_17_out;  // OR_Gate or_3, 3 bits wide
  assign RN_t = and_19_out | and_18_out;  // OR_Gate or_4, 3 bits wide
  or or_5 (or_6_out[1], CN, LSL, ASR, RS, ADDC, SUBC, RR, CR);
  or or_6 (or_6_out[0], ADDC, CR, SUBC, CN);
  Multiplexer #(.width(3), .enable("false")) multiplexer_1 (.in0(3'b000), .in1(RN_t), .out(Rn), .sel(Enable));
  Multiplexer #(.width(3), .enable("false")) multiplexer_2 (.in0(3'b000), .in1(RD_t), .out(Rd), .sel(Enable));
  Multiplexer #(.width(3), .enable("false")) multiplexer_3 (
    .in0(3'b000), .in1(Instruction[5:3]), .out(Rm), .sel(Enable));
  Multiplexer #(.width(4), .enable("false")) multiplexer_4 (
    .in0(4'b0000), .in1(Instruction[9:6]), .out(ALU_Opcode), .sel(Enable));
  Multiplexer #(.width(4), .enable("false")) multiplexer_5 (
    .in0(4'b0000), .in1({2'b11, or_6_out}), .out(Flags_Update_Mask), .sel(Enable));

  // Other names for the same wires on the sheet: b0 = Instruction[0]; b1 = Instruction[1]; b2 = Instruction[2];
  //   b3 = Instruction[3]; b4 = Instruction[4]; b5 = Instruction[5]; b6 = Instruction[6]; b7 = Instruction[7];
  //   b8 = Instruction[8]; b9 = Instruction[9]; b10 = Instruction[10]; b11 = Instruction[11]; b12 = Instruction[12];
  //   b13 = Instruction[13]; b14 = Instruction[14]; b15 = Instruction[15]

  // Notes on the sheet:
  //   Note 2: RSB instruction has Rn as 1st operand.
  //   MUL instruction has Rn as 1st operand and Rdm as 2nd operand
  //   Pull output low on Enable = 0
  //   For simplification purposes, Rm is used for 1st operand both here and in the ALU.
  //   Note: instructions that does not save the result will still have the second operand as the destination register, the ALU will copy the second register to the destination register
endmodule

module Shift_Add_Sub_Mov (
  input  [15:0] Instruction,
  input  Enable,
  output [3:0] Flags_Update_Mask,
  output [2:0] Rm,
  output [2:0] Rn,
  output [2:0] Rd,
  output [4:0] Imm5,
  output [31:0] Imm32,
  output [3:0] ALU_Opcode,
  output Carry,
  output Imm32_Enable
);

  wire AddI, AddR, aluopcdedecoder_sasm_1_carry, ASR, LSL, LSR, Move, not_1_out, not_2_out, not_3_out,
       not_4_out, not_5_out, not_6_out, not_7_out, not_8_out, not_9_out, not_10_out, not_11_out, not_12_out,
       not_13_out, not_14_out, not_15_out, not_16_out, not_17_out, or_1_out, or_2_out, or_3_out, or_4_out,
       or_5_out, or_6_out, or_7_out, or_8_out, or_12_out, or_14_out, SubI, SubR;
  wire [2:0] and_9_out, and_10_out, and_11_out, and_17_out, and_18_out, bit_extender_1_out,
       bit_extender_2_out, bit_extender_3_out, bit_extender_4_out, bit_extender_10_out, bit_extender_12_out,
       Rd1, Rm1, Rn1;
  wire [3:0] aluopcdedecoder_sasm_1_a4, and_15_out, and_16_out, bit_extender_7_out, bit_extender_8_out,
       Flags, or_11_out;
  wire [4:0] bit_extender_6_out, Imm51;
  wire [7:0] and_13_out, bit_extender_5_out;
  wire [31:0] bit_extender_9_out, bit_extender_11_out, Imm321, multiplexer_7_out, subtractor_1_out;

  not not_1 (not_1_out, Instruction[13]);
  not not_2 (not_2_out, Instruction[12]);
  not not_3 (not_3_out, Instruction[11]);
  not not_4 (not_4_out, Instruction[13]);
  not not_5 (not_5_out, Instruction[12]);
  not not_6 (not_6_out, Instruction[13]);
  not not_7 (not_7_out, Instruction[11]);
  not not_8 (not_8_out, Instruction[13]);
  not not_9 (not_9_out, Instruction[10]);
  not not_10 (not_10_out, Instruction[9]);
  not not_11 (not_11_out, Instruction[13]);
  not not_12 (not_12_out, Instruction[10]);
  not not_13 (not_13_out, Instruction[13]);
  not not_14 (not_14_out, Instruction[9]);
  not not_15 (not_15_out, Instruction[13]);
  not not_16 (not_16_out, Instruction[12]);
  not not_17 (not_17_out, Instruction[11]);
  and and_1 (LSL, not_1_out, not_2_out, not_3_out);
  and and_2 (LSR, not_4_out, not_5_out, Instruction[11]);
  and and_3 (ASR, not_6_out, Instruction[12], not_7_out);
  and and_4 (AddR, not_8_out, Instruction[12], Instruction[11], not_9_out, not_10_out);
  and and_5 (SubR, not_11_out, Instruction[12], Instruction[11], not_12_out, Instruction[9]);
  and and_6 (AddI, not_13_out, Instruction[12], Instruction[11], Instruction[10], not_14_out);
  and and_7 (SubI, not_15_out, Instruction[12], Instruction[11], Instruction[10], Instruction[9]);
  and and_8 (Move, Instruction[13], not_16_out, not_17_out);
  or or_1 (or_1_out, AddI, SubI);
  or or_2 (or_2_out, AddR, SubR);
  or or_3 (or_3_out, LSL, LSR, ASR);
  or or_4 (or_4_out, AddI, AddR, SubR, SubI);
  assign bit_extender_1_out = {{2{or_1_out}}, or_1_out};  // Bit_Extender bit_extender_1
  or or_5 (or_5_out, LSL, LSR, ASR);
  or or_6 (or_6_out, LSR, Move);
  or or_7 (or_7_out, LSL, ASR);
  assign bit_extender_2_out = {{2{or_2_out}}, or_2_out};  // Bit_Extender bit_extender_2
  assign bit_extender_3_out = {{2{or_3_out}}, or_3_out};  // Bit_Extender bit_extender_3
  assign bit_extender_4_out = {{2{or_4_out}}, or_4_out};  // Bit_Extender bit_extender_4
  assign and_9_out = bit_extender_1_out & Instruction[8:6];  // AND_Gate and_9, 3 bits wide
  assign bit_extender_5_out = {{7{Move}}, Move};  // Bit_Extender bit_extender_5
  assign bit_extender_6_out = {{4{or_5_out}}, or_5_out};  // Bit_Extender bit_extender_6
  assign bit_extender_7_out = {{3{or_6_out}}, or_6_out};  // Bit_Extender bit_extender_7
  assign bit_extender_8_out = {{3{or_7_out}}, or_7_out};  // Bit_Extender bit_extender_8
  assign and_10_out = bit_extender_2_out & Instruction[8:6];  // AND_Gate and_10, 3 bits wide
  assign and_11_out = bit_extender_3_out & Instruction[5:3];  // AND_Gate and_11, 3 bits wide
  assign Rn1 = bit_extender_4_out & Instruction[5:3];  // AND_Gate and_12, 3 bits wide
  or or_8 (or_8_out, AddI, AddR, SubR, SubI, LSL, LSR, ASR);
  assign bit_extender_9_out = {{29{and_9_out[2]}}, and_9_out};  // Bit_Extender bit_extender_9
  assign and_13_out = bit_extender_5_out & Instruction[7:0];  // AND_Gate and_13, 8 bits wide
  assign Imm51 = bit_extender_6_out & Instruction[10:6];  // AND_Gate and_14, 5 bits wide
  assign and_15_out = bit_extender_7_out & 4'b1100;  // AND_Gate and_15, 4 bits wide
  assign and_16_out = bit_extender_8_out & 4'b1110;  // AND_Gate and_16, 4 bits wide
  assign Rm1 = and_10_out | and_11_out;  // OR_Gate or_9, 3 bits wide
  assign bit_extender_10_out = {{2{or_8_out}}, or_8_out};  // Bit_Extender bit_extender_10
  assign bit_extender_11_out = {{24{and_13_out[7]}}, and_13_out};  // Bit_Extender bit_extender_11
  assign and_17_out = bit_extender_10_out & Instruction[2:0];  // AND_Gate and_17, 3 bits wide
  assign bit_extender_12_out = {{2{Move}}, Move};  // Bit_Extender bit_extender_12
  assign Imm321 = bit_extender_9_out | bit_extender_11_out;  // OR_Gate or_10, 32 bits wide
  assign or_11_out = and_15_out | and_16_out;  // OR_Gate or_11, 4 bits wide
  assign and_18_out = bit_extender_12_out & Instruction[10:8];  // AND_Gate and_18, 3 bits wide
  Multiplexer #(.width(4), .enable("false")) multiplexer_1 (
    .in0(4'b1111), .in1(or_11_out), .out(Flags), .sel(or_12_out));
  or or_12 (or_12_out, LSR, Move, LSL, ASR);
  assign Rd1 = and_17_out | and_18_out;  // OR_Gate or_13, 3 bits wide
  Multiplexer #(.width(4), .enable("false")) multiplexer_2 (
    .in0(4'b0000), .in1(Flags), .out(Flags_Update_Mask), .sel(Enable));
  Multiplexer #(.width(3), .enable("false")) multiplexer_3 (.in0(3'b000), .in1(Rm1), .out(Rm), .sel(Enable));
  Multiplexer #(.width(3), .enable("false")) multiplexer_4 (.in0(3'b000), .in1(Rn1), .out(Rn), .sel(Enable));
  Multiplexer #(.width(3), .enable("false")) multiplexer_5 (.in0(3'b000), .in1(Rd1), .out(Rd), .sel(Enable));
  Multiplexer #(.width(5), .enable("false")) multiplexer_6 (.in0({5{1'b0}}), .in1(Imm51), .out(Imm5), .sel(Enable));
  Multiplexer #(.width(32), .enable("false")) multiplexer_7 (
    .in0({32{1'b0}}), .in1(Imm321), .out(multiplexer_7_out), .sel(Enable));
  Subtractor #(.width(32)) subtractor_1 (
    .a(multiplexer_7_out), .b({32{1'b0}}), .out(subtractor_1_out));  // open: bin, bout
  AluOpcdeDecoder_SASM aluopcdedecoder_sasm_1 (
    .e1(Instruction[13]), .e2(Instruction[12]), .e3(Instruction[11]), .e4(Instruction[10]),
    .e5(Instruction[9]), .a1(aluopcdedecoder_sasm_1_a4[3]), .a2(aluopcdedecoder_sasm_1_a4[2]),
    .a3(aluopcdedecoder_sasm_1_a4[1]), .a4(aluopcdedecoder_sasm_1_a4[0]), .carry(aluopcdedecoder_sasm_1_carry));
  or or_14 (or_14_out, Move, AddI, SubI);
  Multiplexer #(.width(32), .enable("false")) multiplexer_8 (
    .in0(multiplexer_7_out), .in1(subtractor_1_out), .out(Imm32), .sel(Move));
  or or_15 (Imm32_Enable, 1'b0, or_14_out);
  Multiplexer #(.width(4), .enable("false")) multiplexer_9 (
    .in0(4'b0000), .in1(aluopcdedecoder_sasm_1_a4), .out(ALU_Opcode), .sel(Enable));
  Multiplexer #(.enable("false")) multiplexer_10 (
    .in0(1'b0), .in1(aluopcdedecoder_sasm_1_carry), .out(Carry), .sel(Enable));
  AluOpcode_Decoder aluopcode_decoder_1 ();  // open: e0, e1, e2, e3, e4, s0, s1, s2, s3, carry

  // Other names for the same wires on the sheet: B3 = Instruction[3]; B4 = Instruction[4]; B5 = Instruction[5];
  //   B6 = Instruction[6]; B7 = Instruction[7]; B0 = Instruction[0]; B1 = Instruction[1]; B2 = Instruction[2];
  //   B8 = Instruction[8]; B9 = Instruction[9]; B10 = Instruction[10]; Enabled = Enable; B11 = Instruction[11];
  //   B12 = Instruction[12]; B13 = Instruction[13]; B14 = Instruction[14]; B15 = Instruction[15]

  // Notes on the sheet:
  //   Pull output low on Enable = 0
  //   Note: ALU uses Rn register for shifts. Use Rn instead of Rm for shifts (immediate) here too
  //   Note 2: MOV uses RSB ALU opcode with Imm8 reversed so that it is copied to output register
  //   Note 3: Imm32_Enable forces the use of the immediate for Rm register
  //   CHOIX OPERATION
  //   Logical Shift Left
  //   Logical Shift Right
  //   Arithmetic Shift Right
  //   Add Register
  //   Sub Register
  //   Add Immediate
  //   Sub Immediate
  //   Move
  //   SORTIES
  //   Manque les sorties ALU_Opcode & Carry
  //   Enable carry for SUB since it is reversed in ALU
  //   ALU will use Imm32 instead of Rm
endmodule

module Load_Store (
  input  Enable,
  input  Clk,
  input  [15:0] Instruction,
  input  [31:0] Stack_Pointer,
  input  Reset,
  output [2:0] Rd,
  output [2:0] Rm,
  output Store,
  output Load,
  output [31:0] RAM_Addr,
  output PC_Hold
);

  wire and_1_out, d_ff_1_q, d_ff_1_qn, not_1_out;
  wire [2:0] rt;
  wire [7:0] bitselector_1_out, bitselector_3_out;
  wire [31:0] bit_extender_1_out, ram;

  assign bit_extender_1_out = {{24{1'b0}}, bitselector_1_out};  // Bit_Extender bit_extender_1
  BitSelector #(.width(16), .group(8)) bitselector_1 (.in(Instruction), .out(bitselector_1_out), .sel(1'b0));
  BitSelector #(.group(3)) bitselector_2 (.in(bitselector_3_out), .out(rt), .sel(2'b00));
  BitSelector #(.width(16), .group(8)) bitselector_3 (.in(Instruction), .out(bitselector_3_out), .sel(1'b1));
  D_Flip_Flop d_ff_1 (.D(and_1_out), .clk(Clk), .Q(d_ff_1_q), .Qn(d_ff_1_qn), .reset(Reset));  // open: preset
  and and_1 (and_1_out, d_ff_1_qn, Instruction[11]);
  Multiplexer #(.enable("false")) multiplexer_1 (.in0(1'b0), .in1(d_ff_1_q), .out(PC_Hold), .sel(Enable));
  Adder #(.width(32)) adder_1 (.a(bit_extender_1_out), .b(Stack_Pointer), .out(ram));  // open: cin, cout
  Multiplexer #(.width(3), .enable("false")) multiplexer_2 (
    .in0(3'b000), .in1(Instruction[10:8]), .out(Rd), .sel(Enable));
  Multiplexer #(.width(3), .enable("false")) multiplexer_3 (
    .in0(3'b000), .in1(Instruction[10:8]), .out(Rm), .sel(Enable));
  Multiplexer #(.enable("false")) multiplexer_4 (.in0(1'b0), .in1(not_1_out), .out(Store), .sel(Enable));
  not not_1 (not_1_out, Instruction[11]);
  Multiplexer #(.enable("false")) multiplexer_5 (.in0(1'b0), .in1(Instruction[11]), .out(Load), .sel(Enable));
  Multiplexer #(.width(32), .enable("false")) multiplexer_6 (.in0({32{1'b0}}), .in1(ram), .out(RAM_Addr), .sel(Enable));

  // Other names for the same wires on the sheet: clock_ls = Clk; Enab_ls = Enable; inst[15:0] = Instruction;
  //   LorS = Instruction[11]; registre[2:0] = Instruction[10:8]; sp[31:0] = Stack_Pointer

  // Notes on the sheet:
  //   1 si load, 0 si store
  //   Delay load and hold PC for 1 cycle for the RAM to send out requested data 
endmodule

module SP_Address (
  input  Enable,
  input  [15:0] Instruction,
  input  [31:0] Stack_Pointer,
  output Write_Enable,
  output [31:0] New_Stack_Pointer
);

  wire [31:0] adder_1_out, bit_extender_1_out, multiplexer_1_out, subtractor_1_out;

  assign bit_extender_1_out = {{25{Instruction[6]}}, Instruction[6:0]};  // Bit_Extender bit_extender_1
  Adder #(.width(32)) adder_1 (.a(Stack_Pointer), .b(bit_extender_1_out), .out(adder_1_out));  // open: cin, cout
  Subtractor #(.width(32)) subtractor_1 (
    .a(Stack_Pointer), .b(bit_extender_1_out), .out(subtractor_1_out));  // open: bin, bout
  Multiplexer #(.width(32), .enable("false")) multiplexer_1 (
    .in0(adder_1_out), .in1(subtractor_1_out), .out(multiplexer_1_out), .sel(Instruction[7]));
  Multiplexer #(.width(32), .enable("false")) multiplexer_2 (
    .in0({32{1'b0}}), .in1(multiplexer_1_out), .out(New_Stack_Pointer), .sel(Enable));

  assign Write_Enable = Enable;

  // Other names for the same wires on the sheet: en = Enable; b7 = Instruction[7]; SP[31:0] = Stack_Pointer

  // Notes on the sheet:
  //   Pull output low on Enable = 0
  //   b7 = 1? : sub ; add
endmodule

module Flags_APSR (
  input  [3:0] Flags_In,
  input  [3:0] Update_Mask,
  input  Clk,
  input  Rst,
  output [3:0] Flags_Out
);

  wire or_1_out, or_2_out, W;
  wire [3:0] and_1_out;

  or or_1 (or_1_out, Flags_In[0], Flags_In[1]);
  and and_1 (and_1_out[0], Flags_In[0], Update_Mask[0]);
  and and_2 (and_1_out[1], Flags_In[1], Update_Mask[1]);
  and and_3 (and_1_out[2], Flags_In[2], Update_Mask[2]);
  and and_4 (and_1_out[3], Flags_In[3], Update_Mask[3]);
  or or_2 (or_2_out, or_1_out, Flags_In[2]);
  Register #(.width(4), .trigger("falling")) register_1 (.D(and_1_out), .en(W), .clk(Clk), .Q(Flags_Out), .clr(Rst));
  or or_3 (W, or_2_out, Flags_In[3]);

  // Other names for the same wires on the sheet: In0 = Flags_In[0]; In1 = Flags_In[1]; In2 = Flags_In[2];
  //   In3 = Flags_In[3]
endmodule

module AluOpcode_Decoder (
  input  e0,
  input  e1,
  input  e2,
  input  e3,
  input  e4,
  output s0,
  output s1,
  output s2,
  output s3,
  output carry
);

  wire and_2_out, and_3_out, and_4_out, and_5_out, and_6_out, and_7_out, and_8_out, and_9_out, not_1_out,
       not_2_out, not_3_out, not_4_out, not_5_out, not_6_out, not_7_out, not_8_out, not_9_out, not_10_out,
       not_11_out;

  not not_1 (not_1_out, e1);
  not not_2 (not_2_out, e0);
  not not_3 (not_3_out, e1);
  not not_4 (not_4_out, e0);
  not not_5 (not_5_out, e1);
  not not_6 (not_6_out, e0);
  not not_7 (not_7_out, e4);
  not not_8 (not_8_out, e2);
  not not_9 (not_9_out, e0);
  not not_10 (not_10_out, e3);
  not not_11 (not_11_out, e1);
  and and_1 (s0, e0, not_1_out);
  and and_2 (and_2_out, not_2_out, not_3_out);
  and and_3 (and_3_out, e2, e4);
  and and_4 (and_4_out, e0, e2);
  and and_5 (and_5_out, not_4_out, not_5_out, e2);
  and and_6 (and_6_out, not_6_out, e2, not_7_out);
  and and_7 (and_7_out, e0, e1, not_8_out);
  and and_8 (and_8_out, not_9_out, e1, e2, not_10_out);
  and and_9 (and_9_out, e0, not_11_out);
  or or_1 (s2, and_2_out, and_3_out, and_4_out);
  or or_2 (s3, and_5_out, and_6_out, and_7_out);
  or or_3 (carry, and_8_out, and_9_out);

  assign s1 = e1;
endmodule

module AluOpcdeDecoder_SASM (
  input  e1,
  input  e2,
  input  e3,
  input  e4,
  input  e5,
  output a1,
  output a2,
  output a3,
  output a4,
  output carry
);

  wire and_2_out, and_3_out, and_4_out, and_5_out, not_1_out, not_2_out, not_3_out, not_4_out, not_5_out,
       not_6_out, not_7_out;

  not not_1 (not_1_out, e1);
  not not_2 (not_2_out, e1);
  not not_3 (not_3_out, e2);
  not not_4 (not_4_out, e1);
  not not_5 (not_5_out, e2);
  not not_6 (not_6_out, e5);
  not not_7 (not_7_out, e1);
  and and_1 (a2, not_1_out, e2);
  and and_2 (and_2_out, not_2_out, not_3_out);
  and and_3 (and_3_out, not_4_out, e3, e5);
  and and_4 (and_4_out, not_5_out, e3);
  and and_5 (and_5_out, e3, not_6_out);
  and and_6 (carry, not_7_out, e5);
  or or_1 (a3, and_2_out, and_3_out);
  or or_2 (a4, and_4_out, and_5_out, e1);

  assign a1 = e1;
endmodule
