// Logisim project Machine.circ as structural Verilog: 4 circuits, main circuit CPU
module main (
  input  in_1,
  input  GPIO_A1,
  input  GPIO_A3,
  input  GPIO_A5,
  input  GPIO_A7,
  input  GPIO_A9,
  input  GPIO_A11,
  input  GPIO_A13,
  input  GPIO_A15,
  input  GPIO_A17,
  input  GPIO_A19,
  input  GPIO_A21,
  input  GPIO_A23,
  input  GPIO_A25,
  input  GPIO_A27,
  input  GPIO_A29,
  input  GPIO_A31,
  input  GPIO_A33,
  input  GPIO_A35,
  input  GPIO_B1,
  input  GPIO_B3,
  input  GPIO_B5,
  input  GPIO_B7,
  input  GPIO_B9,
  input  GPIO_B11,
  input  GPIO_B13,
  input  GPIO_B15,
  input  GPIO_B17,
  input  GPIO_B19,
  input  GPIO_B21,
  input  GPIO_B23,
  input  GPIO_B25,
  input  GPIO_B27,
  input  GPIO_B29,
  input  GPIO_B31,
  input  GPIO_B33,
  input  GPIO_B35,
  output GPIO_A2,
  output GPIO_A4,
  output GPIO_A6,
  output GPIO_A8,
  output GPIO_A10,
  output GPIO_A12,
  output GPIO_A14,
  output GPIO_A16,
  output GPIO_A18,
  output GPIO_A20,
  output GPIO_A22,
  output GPIO_A24,
  output GPIO_A26,
  output GPIO_A28,
  output GPIO_A30,
  output GPIO_A32,
  output GPIO_A34,
  output GPIO_A36,
  output GPIO_B2,
  output GPIO_B4,
  output GPIO_B6,
  output GPIO_B8,
  output GPIO_B10,
  output GPIO_B12,
  output GPIO_B14,
  output GPIO_B16,
  output GPIO_B18,
  output GPIO_B20,
  output GPIO_B22,
  output GPIO_B24,
  output GPIO_B26,
  output GPIO_B28,
  output GPIO_B30,
  output GPIO_B32,
  output GPIO_B34,
  output GPIO_B36
);

  wire Clk_Button_out, CPU_1_store, Rst_Button_out;
  wire [7:0] RAM_Addr, ROM_Addr;
  wire [15:0] ROMa_data;
  wire [31:0] CPU_1_r0, CPU_1_r1, CPU_1_r2, CPU_1_r3, CPU_1_r4, CPU_1_r5, CPU_1_r6, CPU_1_r7, CPU_1_ram_out,
       RAMa_dout;
  wire [31:8] CPU_1_ram_addr;

  RAM #(.dataWidth(32), .databus("bibus")) RAMa (
    .addr(RAM_Addr), .we(CPU_1_store), .oe(1'b1), .clk(Clk_Button_out), .din(CPU_1_ram_out), .dout(RAMa_dout));
  Clock clock_1 ();  // open: out
  LED A0 (.in(RAMa_dout[0]));
  LED A1 (.in(RAMa_dout[1]));
  LED A2 (.in(RAMa_dout[2]));
  ROM #(.dataWidth(16)) ROMa (.addr(ROM_Addr), .data(ROMa_data));
  Button Clk_Button (.out(Clk_Button_out));
  Button Rst_Button (.out(Rst_Button_out));
  LED A3 (.in(RAMa_dout[3]));
  LED A4 (.in(RAMa_dout[4]));
  LED A5 (.in(RAMa_dout[5]));
  LED A6 (.in(RAMa_dout[6]));
  LED A7 (.in(RAMa_dout[7]));
  LED L0 (.in(CPU_1_r0[0]));
  // Probe on CPU_1_r1
  // Probe on CPU_1_r0
  LED L3 (.in(CPU_1_r0[3]));
  LED L1 (.in(CPU_1_r0[1]));
  LED L2 (.in(CPU_1_r0[2]));
  // Probe on CPU_1_r3
  // Probe on CPU_1_r2
  // Probe on CPU_1_r5
  // Probe on CPU_1_r4
  LED L4 (.in(CPU_1_r0[4]));
  LED L5 (.in(CPU_1_r0[5]));
  // Probe on CPU_1_r7
  // Probe on CPU_1_r6
  CPU CPU_1 (
    .ROM_Addr(ROM_Addr), .RAM_In(RAMa_dout), .R3(CPU_1_r3), .R7(CPU_1_r7), .R2(CPU_1_r2), .R6(CPU_1_r6),
    .RAM_Addr({CPU_1_ram_addr, RAM_Addr}), .R1(CPU_1_r1), .R5(CPU_1_r5), .ROM_In(ROMa_data), .R0(CPU_1_r0),
    .R4(CPU_1_r4), .Clk(Clk_Button_out), .RAM_Out(CPU_1_ram_out), .Reset(Rst_Button_out), .Store(CPU_1_store));
  LED L6 (.in(CPU_1_r0[6]));
  LED L7 (.in(CPU_1_r0[7]));
  LED LED_1 (.in(RAM_Addr[0]));
  LED LED_2 (.in(RAM_Addr[1]));
  LED LED_3 (.in(RAM_Addr[2]));
  LED LED_4 (.in(RAM_Addr[3]));
  LED LED_5 (.in(RAM_Addr[4]));
  LED LED_6 (.in(RAM_Addr[5]));
  LED LED_7 (.in(RAM_Addr[6]));
  LED LED_8 (.in(RAM_Addr[7]));

  // Notes on the sheet:
  //   contents of ROMa (hex, n*v repeats v):
  //   9902 b002 9902 b081 9902
  //   Use only 8 bit adresses
  //   VCC 5V
  //   VCC 3.3V
  //   VCC 5V
  //   VCC 3.3V
  //   GROUND
  //   GROUND
  //   GROUND
  //   GROUND
endmodule

module CPU (
  input  [31:0] RAM_In,
  input  [15:0] ROM_In,
  input  Clk,
  input  Reset,
  output [7:0] ROM_Addr,
  output [31:0] R3,
  output [31:0] R7,
  output [31:0] R2,
  output [31:0] R6,
  output [31:0] RAM_Addr,
  output [31:0] R1,
  output [31:0] R5,
  output [31:0] R0,
  output [31:0] R4,
  output [31:0] RAM_Out,
  output Store
);

  wire Controller_1_carry, Controller_1_load, controlregwrite_1_write, imm5e, imm32e, or_1_out, vImm;
  wire [2:0] Controller_1_rd, Controller_1_rm, Controller_1_rn;
  wire [3:0] ALU_1_flags, opcode;
  wire [4:0] bitselector_1_out, Controller_1_imm5, multiplexer_2_out;
  wire [31:0] ALU_1_s, Controller_1_imm32, multiplexer_1_out, multiplexer_3_out, multiplexer_4_out,
       multiplexer_5_out, register_1_q, Regs_1_bout;

  Multiplexer #(.width(32), .enable("false")) multiplexer_1 (
    .in0(register_1_q), .in1(RAM_In), .out(multiplexer_1_out), .sel(Controller_1_load));
  Controller Controller_1 (
    .Imm5(Controller_1_imm5), .Imm32(Controller_1_imm32), .Rn(Controller_1_rn), .Inst(ROM_In),
    .ALU_Opcode(opcode), .Rd(Controller_1_rd), .Flags(ALU_1_flags), .Rm(Controller_1_rm), .PC(ROM_Addr),
    .Imm32_Enable(imm32e), .DP_Shift(imm5e), .Carry(Controller_1_carry), .RAM_Addr(RAM_Addr),
    .Load(Controller_1_load), .Store(Store), .Clk(Clk), .Reset(Reset));
  or or_1 (or_1_out, imm5e, imm32e);
  BitSelector #(.width(32), .group(5)) bitselector_1 (.in(RAM_Out), .out(bitselector_1_out), .sel(3'b000));
  BancRegistre Regs_1 (
    .Clk(Clk), .Reset(Reset), .DataIn(multiplexer_1_out), .RegB(Controller_1_rn), .BOut(Regs_1_bout),
    .AOut(RAM_Out), .R0(R0), .R1(R1), .R2(R2), .R3(R3), .R4(R4), .R5(R5), .R6(R6), .R7(R7),
    .RegA(Controller_1_rm), .RegDest(Controller_1_rd));
  Multiplexer #(.width(5), .enable("false")) multiplexer_2 (
    .in0(bitselector_1_out), .in1(Controller_1_imm5), .out(multiplexer_2_out), .sel(imm5e));
  Multiplexer #(.width(32), .enable("false")) multiplexer_3 (
    .in0(RAM_Out), .in1(Controller_1_imm32), .out(multiplexer_3_out), .sel(imm32e));
  ALU ALU_1 (
    .S(ALU_1_s), .Flags(ALU_1_flags), .A(multiplexer_4_out), .B(multiplexer_5_out),
    .Shift(multiplexer_2_out), .CarryIn(Controller_1_carry), .Codop(opcode));
  ControlRegWrite controlregwrite_1 (
    .a1(opcode[3]), .a2(opcode[2]), .a3(opcode[1]), .a4(opcode[0]), .write(controlregwrite_1_write));
  testSubCImm32 testsubcimm32_1 (
    .e1(opcode[3]), .e2(opcode[2]), .e3(opcode[1]), .e4(opcode[0]), .imm32(or_1_out), .v(vImm));
  Register #(.width(32)) register_1 (
    .D(ALU_1_s), .en(controlregwrite_1_write), .clk(Clk), .Q(register_1_q), .clr(Reset));
  Multiplexer #(.width(32), .enable("false")) multiplexer_4 (
    .in0(multiplexer_3_out), .in1(Regs_1_bout), .out(multiplexer_4_out), .sel(vImm));
  Multiplexer #(.width(32), .enable("false")) multiplexer_5 (
    .in0(Regs_1_bout), .in1(multiplexer_3_out), .out(multiplexer_5_out), .sel(vImm));

  // Notes on the sheet:
  //   Inverse a et b de l'alu pour un substract immediate
  //   Ajout d'un registre pour palier au fait que l'on ne peut empêcher d'écrire dans un registre (pour TST, CMP et CMN)
  //   On desactive l'ecriture pour TST, CMP et CMN
endmodule

module ControlRegWrite (
  input  a1,
  input  a2,
  input  a3,
  input  a4,
  output write
);

  wire and_1_out, not_1_out, not_2_out;

  not not_1 (not_1_out, a3);
  not not_2 (not_2_out, a1);
  and and_1 (and_1_out, not_1_out, a4);
  or or_1 (write, not_2_out, and_1_out, a2);
endmodule

module testSubCImm32 (
  input  e1,
  input  e2,
  input  e3,
  input  e4,
  input  imm32,
  output v
);

  wire and_1_out, and_2_out, and_3_out, not_1_out, not_2_out, not_3_out, not_4_out, not_5_out, not_6_out,
       not_7_out, not_8_out, not_9_out;

  not not_1 (not_1_out, e1);
  not not_2 (not_2_out, e2);
  not not_3 (not_3_out, imm32);
  not not_4 (not_4_out, e1);
  not not_5 (not_5_out, e3);
  not not_6 (not_6_out, e4);
  not not_7 (not_7_out, imm32);
  not not_8 (not_8_out, e1);
  not not_9 (not_9_out, e4);
  and and_1 (and_1_out, not_1_out, not_2_out, e3, not_3_out);
  and and_2 (and_2_out, not_4_out, e2, not_5_out, not_6_out, not_7_out);
  and and_3 (and_3_out, not_8_out, e2, e3, not_9_out, imm32);
  or or_1 (v, and_1_out, and_2_out, and_3_out);
endmodule
